# Fritzing sketch LDR_Ciruit Diagram FritzingFiles (saved by Fritzing 0.9.3b)

parts:
  R1 = Photocell (LDR) [package=THT]
  R2 = Resistor [tolerance=±5% resistance=100 package=THT]
  Part1 = Arduino Uno (Rev3)

nets:
  N1: R1.pin_0, Part1.5V
  N2: R1.pin_1, R2.Pin_0
