# Fritzing sketch LDR_and_RGB_LED_Fritzing_File (saved by Fritzing 0.9.3b)
breadboards: 1

parts:
  R2 = Photocell (LDR) [package=THT]
  Part1 = Arduino Uno (Rev3)
  R1 = Resistor [tolerance=±20% resistance=1k package=THT]
  LED1 = RGB LED (com. cathode, rgb) [package="5 mm [THT]"]
  R3 = Resistor [tolerance=±5% resistance=220 package=THT]
  R4 = Resistor [tolerance=±5% resistance=220 package=THT]
  R5 = Resistor [tolerance=±5% resistance=220 package=THT]

nets:
  N1: R2.pin_0, Part1.A0, R1.Pin_1
  N2: R2.pin_1, Part1.5V
  N3: Part1.D9_PWM, R4.Pin_1
  N4: Part1.D10_PWM/SS, R5.Pin_1
  N5: Part1.D11_PWM/MOSI, R3.Pin_1
  N6: Part1.GND, R1.Pin_0
  N7: LED1.red_anode, R3.Pin_0
  N8: LED1.green_anode, R5.Pin_0
  N9: LED1.blue_anode, R4.Pin_0
